# Fritzing sketch 01_flash_leds (saved by Fritzing 1.0.5)
breadboards: 1

parts:
  RP1 = WaveShare RP2350 LCD-1.28 Connector
  R1 = Resistor [tolerance=±5% power=0.25W resistance=220 package=THT]
  LED1 = LED - 5mm [color="Red (633nm)" current=0.030A package="5 mm [THT]"]

nets:
  N1: RP1.22, R1.Pin_0
  N2: RP1.GND, LED1.cathode
  N3: R1.Pin_1, LED1.anode

custom parts:
  WaveShare RP2350 LCD-1.28 Connector: WaveShare RP2350 LCD-1.28 on a PCB designed at the HS-Esslingen
