# Fritzing sketch RP2350_pull_down_external (saved by Fritzing 1.0.5)
breadboards: 1

parts:
  RP1 = WaveShare RP2350 LCD-1.28 Connector
  R1 = Isolated5 Resistor-5 (SIP-10) [tolerance=±5% resistance=100 package=SIP-10]
  LED2 = RGB LED (com. anode, rbg) [color="Red (633nm)" current=0.030A package="5 mm [THT]"]
  S1 = Pushbutton [package="[THT]"]
  R2 = Resistor [tolerance=±5% power=0.25W resistance=10k package=THT]
  R3 = Resistor [tolerance=±5% power=0.25W resistance=4.7k package=THT]
  R4 = Resistor [tolerance=±5% power=0.25W resistance=10k package=THT]

nets:
  N1: RP1.5, R1.Pin_4
  N2: RP1.4, R1.Pin_2
  N3: RP1.3, R1.Pin_0
  N4: RP1.13, S1.Pin_1, S1.Pin_2, R2.Pin_0, R3.Pin_0
  N5: RP1.Vcc, R2.Pin_1
  N6: RP1.GND, LED2.common_anode, R3.Pin_1, R4.Pin_1
  N7: R1.Pin_1, LED2.green_cathode
  N8: R1.Pin_3, LED2.blue_cathode
  N9: R1.Pin_5, LED2.red_cathode
  N10: S1.Pin_3, S1.Pin_4, R4.Pin_0

notes:
  Upper Power-rail:
  + is derived using a voltage divider
  (Spannungsteiler10kOhm and 4,7kOhm)
  Lower Power-rail:
  + is driven by IOVDD (5V)

custom parts:
  WaveShare RP2350 LCD-1.28 Connector: WaveShare RP2350 LCD-1.28 on a PCB designed at the HS-Esslingen
  Isolated5 Resistor-5 (SIP-10): A resistor array is a single package which contains more than one resistor. They are typically used for convenience when several resistors are needed together in the same place in a circuit.
