# Fritzing sketch 03_gpio_dcf77 (saved by Fritzing 1.0.5)
breadboards: 1

parts:
  RP1 = WaveShare RP2350 LCD-1.28 Connector
  R1 = Isolated5 Resistor-5 (SIP-10) [tolerance=±5% resistance=100 package=SIP-10]
  LED2 = RGB LED (com. anode, rbg) [color="Red (633nm)" current=0.030A package="5 mm [THT]"]
  R2 = Resistor [tolerance=±5% resistance=4.7k package="1206 [SMD]"]
  R3 = Resistor [tolerance=±5% resistance=10k package="1206 [SMD]"]
  DCF1 = KundoXT DCF77 antenna
  U1 = LM-324N quadruple operational Amp [part_number=LM324N package="DIP (Dual Inline) [THT]"]
  part = LM-324N quadruple operational Amp [part_number=LM324N package="DIP (Dual Inline) [THT]"]  # not connected
  U1_1 = LM-324N quadruple operational Amp [part_number=LM324N package="DIP (Dual Inline) [THT]"]  # not connected
  U1_2 = LM-324N quadruple operational Amp [part_number=LM324N package="DIP (Dual Inline) [THT]"]  # not connected
  U1_3 = LM-324N quadruple operational Amp [part_number=LM324N package="DIP (Dual Inline) [THT]"]  # not connected
  U1_4 = LM-324N quadruple operational Amp [part_number=LM324N package="DIP (Dual Inline) [THT]"]  # not connected
  R4_-_Feedback_1IN-_&_1IN+ = Resistor [tolerance=±5% power=0.25W resistance=4.7k package=THT]
  R5_-_Pull-Down_1OUT_to_GND = Resistor [tolerance=±5% power=0.25W resistance=220 package=THT]

nets:
  N1: RP1.5, R1.Pin_4
  N2: RP1.4, R1.Pin_2
  N3: RP1.3, R1.Pin_0
  N4: RP1.1, U1.connector0, R5_-_Pull-Down_1OUT_to_GND.Pin_0
  N5: RP1.ADC, RP1.Vcc, R2.Pin_1
  GND: RP1.GND, LED2.common_anode, R3.Pin_1, DCF1.GND, DCF1.Enable, U1.connector10, R5_-_Pull-Down_1OUT_to_GND.Pin_1
  N6: R1.Pin_1, LED2.green_cathode
  N7: R1.Pin_3, LED2.blue_cathode
  N8: R1.Pin_5, LED2.red_cathode
  N9: R2.Pin_0, R3.Pin_0, DCF1.Signal, U1.connector3
  N10: DCF1.+UB, U1.connector1, R4_-_Feedback_1IN-_&_1IN+.Pin_1
  N11: U1.connector2, R4_-_Feedback_1IN-_&_1IN+.Pin_0

notes:
  LM234 Op-AMP
  Pin1: 1OUT is now lower-right
  Pin2: 1IN-
  Pin3: 1IN+

custom parts:
  WaveShare RP2350 LCD-1.28 Connector: WaveShare RP2350 LCD-1.28 on a PCB designed at the HS-Esslingen
  Isolated5 Resistor-5 (SIP-10): A resistor array is a single package which contains more than one resistor. They are typically used for convenience when several resistors are needed together in the same place in a circuit.
  KundoXT DCF77 antenna: KundoXT DCF77 antenna and PCB available from Reichelt
  LM-324N quadruple operational Amp: LM-324N Quadruple Op-Amp
  LM-324N quadruple operational Amp: LM-324N Quadruple Op-Amp
  LM-324N quadruple operational Amp: LM-324N Quadruple Op-Amp
  LM-324N quadruple operational Amp: LM-324N Quadruple Op-Amp
  LM-324N quadruple operational Amp: LM-324N Quadruple Op-Amp
  LM-324N quadruple operational Amp: LM-324N Quadruple Op-Amp
