# Fritzing sketch 30_pwm_rgb_led (saved by Fritzing 1.0.5)
breadboards: 1

parts:
  RP1 = WaveShare RP2350 LCD-1.28 Connector
  LED1 = RGB LED (com. cathode, rbg) [color="Red (633nm)" current=0.030A package="5 mm [THT]"]
  R1 = Resistor [tolerance=±5% power=0.25W resistance=220 package=THT]
  R2 = Resistor [tolerance=±5% power=0.25W resistance=220 package=THT]
  R3 = Resistor [tolerance=±5% power=0.25W resistance=220 package=THT]

nets:
  N1: RP1.2, R1.Pin_0
  N2: RP1.1, R2.Pin_0
  N3: RP1.0, R3.Pin_0
  N4: RP1.GND, LED1.common_cathode
  N5: LED1.red_anode, R3.Pin_1
  N6: LED1.blue_anode, R2.Pin_1
  N7: LED1.green_anode, R1.Pin_1

custom parts:
  WaveShare RP2350 LCD-1.28 Connector: WaveShare RP2350 LCD-1.28 on a PCB designed at the HS-Esslingen
