# Fritzing sketch board_setup (saved by Fritzing 1.0.5)
breadboards: 1

parts:
  RP1 = WaveShare RP2350 LCD-1.28 Connector
  R1 = Isolated5 Resistor-5 (SIP-10) [tolerance=±5% resistance=100 package=SIP-10]
  LED2 = RGB LED (com. anode, rbg) [color="Red (633nm)" current=0.030A package="5 mm [THT]"]
  Part1 = Thumb Joystick
  R3 = Resistor [tolerance=±5% power=0.25W resistance=10k package=THT]
  R4 = Resistor [tolerance=±5% power=0.25W resistance=4.7k package=THT]
  S2 = Pushbutton [package="[THT]"]

nets:
  N1: RP1.5, R1.Pin_4
  N2: RP1.4, R1.Pin_2
  N3: RP1.3, R1.Pin_0
  GND: RP1.0, RP1.GND, LED2.common_anode, Part1.GND, R4.Pin_1, S2.Pin_1, S2.Pin_2
  N4: RP1.16, Part1.HORZ
  N5: RP1.ADC, RP1.Vcc, Part1.SEL, R3.Pin_1
  N6: RP1.27, Part1.VCC
  N7: RP1.26, Part1.VERT
  N8: R1.Pin_1, LED2.green_cathode
  N9: R1.Pin_3, LED2.blue_cathode
  N10: R1.Pin_5, LED2.red_cathode
  N11: R3.Pin_0, R4.Pin_0
  N12: S2.Pin_3, S2.Pin_4

custom parts:
  WaveShare RP2350 LCD-1.28 Connector: WaveShare RP2350 LCD-1.28 on a PCB designed at the HS-Esslingen
  Isolated5 Resistor-5 (SIP-10): A resistor array is a single package which contains more than one resistor. They are typically used for convenience when several resistors are needed together in the same place in a circuit.
