# Fritzing sketch breadboard_setup (saved by Fritzing 1.0.5)
breadboards: 1

parts:
  RP1 = WaveShare RP2350 LCD-1.28 Connector
  R1 = Isolated5 Resistor-5 (SIP-10) [tolerance=±5% resistance=100 package=SIP-10]
  LED2 = RGB LED (com. anode, rbg) [color="Red (633nm)" current=0.030A package="5 mm [THT]"]
  LED3 = LED - 5mm [color="Red (633nm)" current=0.030A package="5 mm [THT]"]

nets:
  N1: RP1.5, R1.Pin_4
  N2: RP1.4, R1.Pin_2
  N3: RP1.3, R1.Pin_0
  N4: RP1.1, R1.Pin_8
  N5: RP1.GND, LED2.common_anode, LED3.anode
  N6: R1.Pin_1, LED2.green_cathode
  N7: R1.Pin_3, LED2.blue_cathode
  N8: R1.Pin_5, LED2.red_cathode
  N9: R1.Pin_9, LED3.cathode

notes:
  The power-rail + is connected to IOVDD (5V!), this should not
  be used as input into GPIO (3.3V)
  The GND/- is connected to USB-GND

custom parts:
  WaveShare RP2350 LCD-1.28 Connector: WaveShare RP2350 LCD-1.28 on a PCB designed at the HS-Esslingen
  Isolated5 Resistor-5 (SIP-10): A resistor array is a single package which contains more than one resistor. They are typically used for convenience when several resistors are needed together in the same place in a circuit.
